// Logisim project full_arithmatic_with_decoder_selector.circ as structural Verilog: 1 circuit, main circuit main
module main (
  input  in_1,
  input  in_2,
  input  in_3,
  input  in_4,
  input  in_5,
  input  in_6,
  input  in_7,
  input  in_8,
  input  in_9,
  input  in_10,
  input  in_11,
  input  in_12,
  input  in_13,
  input  in_14,
  input  in_15,
  input  in_16,
  input  in_17,
  input  in_18,
  input  in_19,
  output out_20,
  output out_21,
  output out_22,
  output out_23,
  output out_24,
  output out_25,
  output out_26,
  output out_27,
  output out_28,
  output out_29,
  output out_30,
  output out_31,
  output out_32,
  output out_33,
  output out_34
);

  wire adder_2_cout, adder_3_cout, adder_4_cout, adder_5_cout, adder_6_cout, adder_7_cout, adder_8_cout,
       and_1_out, and_2_out, and_6_out, and_7_out, and_11_out, and_12_out, and_13_out, and_14_out,
       and_15_out, and_16_out, and_17_out, and_18_out, and_19_out, and_20_out, and_21_out, and_22_out,
       and_23_out, and_24_out, or_1_out, or_2_out, or_3_out, or_4_out, or_5_out, or_6_out, or_7_out,
       or_8_out, or_9_out;

  and and_1 (and_1_out, ~in_1, ~in_2, in_3);  // AND_Gate
  and and_2 (and_2_out, ~in_1, ~in_2, ~in_3);  // AND_Gate
  or or_1 (or_1_out, ~and_2_out, and_1_out);  // OR_Gate
  and and_3 (out_20, ~in_1, in_2, ~in_3);  // AND_Gate
  and and_4 (out_21, ~in_1, in_2, in_3);  // AND_Gate
  and and_5 (out_22, in_1, ~in_2, ~in_3);  // AND_Gate
  and and_6 (and_6_out, or_1_out, ~in_12);  // AND_Gate
  and and_7 (and_7_out, in_12, ~or_1_out);  // AND_Gate
  or or_2 (or_2_out, and_6_out, and_7_out);
  Adder #(.width(1)) adder_1 (.a(in_4), .b(or_2_out), .out(out_27), .cin(adder_2_cout), .cout(out_26));
  and and_8 (out_23, in_1, ~in_2, in_3);  // AND_Gate
  and and_9 (out_25, in_1, in_2, in_3);
  and and_10 (out_24, in_1, in_2, ~in_3);  // AND_Gate
  and and_11 (and_11_out, or_1_out, ~in_13);  // AND_Gate
  and and_12 (and_12_out, in_13, ~or_1_out);  // AND_Gate
  or or_3 (or_3_out, and_11_out, and_12_out);
  Adder #(.width(1)) adder_2 (.a(in_5), .b(or_3_out), .out(out_28), .cin(adder_3_cout), .cout(adder_2_cout));
  and and_13 (and_13_out, or_1_out, ~in_14);  // AND_Gate
  and and_14 (and_14_out, in_14, ~or_1_out);  // AND_Gate
  or or_4 (or_4_out, and_13_out, and_14_out);
  Adder #(.width(1)) adder_3 (.a(in_6), .b(or_4_out), .out(out_29), .cin(adder_4_cout), .cout(adder_3_cout));
  and and_15 (and_15_out, in_15, ~or_1_out);  // AND_Gate
  and and_16 (and_16_out, or_1_out, ~in_15);  // AND_Gate
  or or_5 (or_5_out, and_16_out, and_15_out);
  Adder #(.width(1)) adder_4 (.a(in_7), .b(or_5_out), .out(out_30), .cin(adder_5_cout), .cout(adder_4_cout));
  and and_17 (and_17_out, or_1_out, ~in_16);  // AND_Gate
  and and_18 (and_18_out, in_16, ~or_1_out);  // AND_Gate
  or or_6 (or_6_out, and_17_out, and_18_out);
  Adder #(.width(1)) adder_5 (.a(in_8), .b(or_6_out), .out(out_31), .cin(adder_6_cout), .cout(adder_5_cout));
  and and_19 (and_19_out, in_17, ~or_1_out);  // AND_Gate
  and and_20 (and_20_out, or_1_out, ~in_17);  // AND_Gate
  or or_7 (or_7_out, and_20_out, and_19_out);
  Adder #(.width(1)) adder_6 (.a(in_9), .b(or_7_out), .out(out_32), .cin(adder_7_cout), .cout(adder_6_cout));
  and and_21 (and_21_out, or_1_out, ~in_18);  // AND_Gate
  and and_22 (and_22_out, in_18, ~or_1_out);  // AND_Gate
  or or_8 (or_8_out, and_21_out, and_22_out);
  Adder #(.width(1)) adder_7 (.a(in_10), .b(or_8_out), .out(out_33), .cin(adder_8_cout), .cout(adder_7_cout));
  and and_23 (and_23_out, or_1_out, ~in_19);  // AND_Gate
  and and_24 (and_24_out, in_19, ~or_1_out);  // AND_Gate
  or or_9 (or_9_out, and_23_out, and_24_out);
  Adder #(.width(1)) adder_8 (.a(in_11), .b(or_9_out), .out(out_34), .cin(or_1_out), .cout(adder_8_cout));

  // Notes on the sheet:
  //   000 == Addition
  //   001 == Subtraction
  //   010 == Multiplication
  //   011 == Division
  //   100 == Modulus
  //   101 == Equal To
  //   110 == Greater Than
  //   111 == Less Than
endmodule
