// Logisim project lc_3_setup.circ as structural Verilog
module _16bit_reg_1 (
  input  [15:0] In,
  input  WE,
  output Out15,
  output Out13,
  output Out11,
  output Out9,
  output Out7,
  output Out5,
  output Out3,
  output Out1,
  output Out14,
  output Out12,
  output Out10,
  output Out8,
  output Out6,
  output Out4,
  output Out2,
  output Out0
);

  wire nand_1_out, nand_2_out, nand_3_out, nand_4_out, nand_6_out, nand_7_out, nand_8_out, nand_10_out,
       nand_11_out, nand_12_out, nand_14_out, nand_15_out, nand_16_out, nand_18_out, nand_19_out,
       nand_21_out, nand_22_out, nand_23_out, nand_25_out, nand_26_out, nand_28_out, nand_29_out,
       nand_30_out, nand_31_out, nand_33_out, nand_34_out, nand_35_out, nand_36_out, nand_37_out,
       nand_39_out, nand_40_out, nand_42_out, nand_43_out, nand_44_out, nand_46_out, nand_47_out,
       nand_48_out, nand_50_out, nand_51_out, nand_53_out, nand_54_out, nand_56_out, nand_57_out,
       nand_58_out, nand_60_out, nand_61_out, nand_62_out, nand_64_out;

  nand nand_1 (nand_1_out, WE, ~In[15]);  // NAND_Gate
  nand nand_2 (nand_2_out, nand_1_out, Out15);
  nand nand_3 (nand_3_out, WE, ~In[14]);  // NAND_Gate
  nand nand_4 (nand_4_out, In[15], WE);
  nand nand_5 (Out15, nand_2_out, nand_4_out);
  nand nand_6 (nand_6_out, nand_3_out, Out14);
  nand nand_7 (nand_7_out, In[14], WE);
  nand nand_8 (nand_8_out, WE, ~In[13]);  // NAND_Gate
  nand nand_9 (Out14, nand_6_out, nand_7_out);
  nand nand_10 (nand_10_out, nand_8_out, Out13);
  nand nand_11 (nand_11_out, In[13], WE);
  nand nand_12 (nand_12_out, WE, ~In[12]);  // NAND_Gate
  nand nand_13 (Out13, nand_10_out, nand_11_out);
  nand nand_14 (nand_14_out, nand_12_out, Out12);
  nand nand_15 (nand_15_out, WE, ~In[11]);  // NAND_Gate
  nand nand_16 (nand_16_out, In[12], WE);
  nand nand_17 (Out12, nand_14_out, nand_16_out);
  nand nand_18 (nand_18_out, nand_15_out, Out11);
  nand nand_19 (nand_19_out, In[11], WE);
  nand nand_20 (Out11, nand_18_out, nand_19_out);
  nand nand_21 (nand_21_out, In[10], WE);
  nand nand_22 (nand_22_out, WE, ~In[10]);  // NAND_Gate
  nand nand_23 (nand_23_out, nand_22_out, Out10);
  nand nand_24 (Out10, nand_23_out, nand_21_out);
  nand nand_25 (nand_25_out, In[9], WE);
  nand nand_26 (nand_26_out, WE, ~In[9]);  // NAND_Gate
  nand nand_27 (Out9, nand_28_out, nand_25_out);
  nand nand_28 (nand_28_out, nand_26_out, Out9);
  nand nand_29 (nand_29_out, WE, ~In[8]);  // NAND_Gate
  nand nand_30 (nand_30_out, In[8], WE);
  nand nand_31 (nand_31_out, nand_29_out, Out8);
  nand nand_32 (Out8, nand_31_out, nand_30_out);
  nand nand_33 (nand_33_out, WE, ~In[7]);  // NAND_Gate
  nand nand_34 (nand_34_out, nand_33_out, Out7);
  nand nand_35 (nand_35_out, WE, ~In[6]);  // NAND_Gate
  nand nand_36 (nand_36_out, In[7], WE);
  nand nand_37 (nand_37_out, nand_35_out, Out6);
  nand nand_38 (Out7, nand_34_out, nand_36_out);
  nand nand_39 (nand_39_out, WE, ~In[5]);  // NAND_Gate
  nand nand_40 (nand_40_out, In[6], WE);
  nand nand_41 (Out6, nand_37_out, nand_40_out);
  nand nand_42 (nand_42_out, nand_39_out, Out5);
  nand nand_43 (nand_43_out, In[5], WE);
  nand nand_44 (nand_44_out, WE, ~In[4]);  // NAND_Gate
  nand nand_45 (Out5, nand_42_out, nand_43_out);
  nand nand_46 (nand_46_out, nand_44_out, Out4);
  nand nand_47 (nand_47_out, WE, ~In[3]);  // NAND_Gate
  nand nand_48 (nand_48_out, In[4], WE);
  nand nand_49 (Out4, nand_46_out, nand_48_out);
  nand nand_50 (nand_50_out, nand_47_out, Out3);
  nand nand_51 (nand_51_out, In[3], WE);
  nand nand_52 (Out3, nand_50_out, nand_51_out);
  nand nand_53 (nand_53_out, In[2], WE);
  nand nand_54 (nand_54_out, WE, ~In[2]);  // NAND_Gate
  nand nand_55 (Out2, nand_56_out, nand_53_out);
  nand nand_56 (nand_56_out, nand_54_out, Out2);
  nand nand_57 (nand_57_out, WE, ~In[1]);  // NAND_Gate
  nand nand_58 (nand_58_out, In[1], WE);
  nand nand_59 (Out1, nand_60_out, nand_58_out);
  nand nand_60 (nand_60_out, nand_57_out, Out1);
  nand nand_61 (nand_61_out, WE, ~In[0]);  // NAND_Gate
  nand nand_62 (nand_62_out, In[0], WE);
  nand nand_63 (Out0, nand_64_out, nand_62_out);
  nand nand_64 (nand_64_out, nand_61_out, Out0);
endmodule

module _16bit_reg_selector (
  input  In,
  input  In_2,
  input  In_3,
  input  In_4,
  input  In_5,
  input  In_6,
  input  In_7,
  input  In_8,
  input  In_9,
  input  In_10,
  input  In_11,
  input  In_12,
  input  In_13,
  input  In_14,
  input  In_15,
  input  In_16,
  input  WE,
  output [15:0] Out
);

  and and_1 (Out[15], WE, In);
  and and_2 (Out[13], WE, In_3);
  and and_3 (Out[14], WE, In_2);
  and and_4 (Out[12], WE, In_4);
  and and_5 (Out[10], WE, In_6);
  and and_6 (Out[11], WE, In_5);
  and and_7 (Out[8], WE, In_8);
  and and_8 (Out[7], WE, In_9);
  and and_9 (Out[9], WE, In_7);
  and and_10 (Out[6], WE, In_10);
  and and_11 (Out[5], WE, In_11);
  and and_12 (Out[3], WE, In_13);
  and and_13 (Out[2], WE, In_14);
  and and_14 (Out[4], WE, In_12);
  and and_15 (Out[1], WE, In_15);
  and and_16 (Out[0], WE, In_16);
endmodule

module inst_reg (
  input  [8:0] in_1,
  input  [2:0] in_2,
  input  in_3,
  input  in_4,
  output [15:0] out_5
);

  wire and_1_out, and_2_out, and_3_out, and_5_out, and_7_out, and_9_out, and_11_out, and_13_out, and_15_out,
       n16bit_reg_1_1_out0, n16bit_reg_1_1_out1, n16bit_reg_1_1_out2, n16bit_reg_1_1_out3,
       n16bit_reg_1_1_out4, n16bit_reg_1_1_out5, n16bit_reg_1_1_out6, n16bit_reg_1_1_out7,
       n16bit_reg_1_1_out8, n16bit_reg_1_1_out9, n16bit_reg_1_1_out10, n16bit_reg_1_1_out11,
       n16bit_reg_1_1_out12, n16bit_reg_1_1_out13, n16bit_reg_1_1_out14, n16bit_reg_1_1_out15;

  and and_1 (and_1_out, ~in_2[0], ~in_2[1], ~in_2[2]);  // AND_Gate
  and and_2 (and_2_out, and_1_out, in_3);
  and and_3 (and_3_out, in_2[0], ~in_2[1], ~in_2[2]);  // AND_Gate
  // AND_Gate and_4 has open pins: in0=and_3_out, in1=in_3, out=open
  and and_5 (and_5_out, ~in_2[0], in_2[1], ~in_2[2]);  // AND_Gate
  // AND_Gate and_6 has open pins: in0=and_5_out, in1=in_3, out=open
  and and_7 (and_7_out, in_2[0], in_2[1], ~in_2[2]);  // AND_Gate
  // AND_Gate and_8 has open pins: in0=and_7_out, in1=in_3, out=open
  and and_9 (and_9_out, ~in_2[0], ~in_2[1], in_2[2]);  // AND_Gate
  // AND_Gate and_10 has open pins: in0=and_9_out, in1=in_3, out=open
  and and_11 (and_11_out, in_2[0], ~in_2[1], in_2[2]);  // AND_Gate
  // AND_Gate and_12 has open pins: in0=and_11_out, in1=in_3, out=open
  and and_13 (and_13_out, ~in_2[0], in_2[1], in_2[2]);  // AND_Gate
  // AND_Gate and_14 has open pins: in0=and_13_out, in1=in_3, out=open
  and and_15 (and_15_out, in_2[0], in_2[1], in_2[2]);
  // AND_Gate and_16 has open pins: in0=and_15_out, in1=in_3, out=open
  _16bit_reg_1 u_16bit_reg_1_1 (
    .WE(and_2_out), .In({4'b0001, in_1[8:3], 3'b000, in_1[2:0]}), .Out15(n16bit_reg_1_1_out15),
    .Out14(n16bit_reg_1_1_out14), .Out13(n16bit_reg_1_1_out13), .Out12(n16bit_reg_1_1_out12),
    .Out11(n16bit_reg_1_1_out11), .Out10(n16bit_reg_1_1_out10), .Out9(n16bit_reg_1_1_out9),
    .Out8(n16bit_reg_1_1_out8), .Out7(n16bit_reg_1_1_out7), .Out6(n16bit_reg_1_1_out6),
    .Out5(n16bit_reg_1_1_out5), .Out4(n16bit_reg_1_1_out4), .Out3(n16bit_reg_1_1_out3),
    .Out2(n16bit_reg_1_1_out2), .Out1(n16bit_reg_1_1_out1), .Out0(n16bit_reg_1_1_out0));
  _16bit_reg_selector u_16bit_reg_selector_1 (
    .WE(and_1_out), .In(n16bit_reg_1_1_out15), .In_2(n16bit_reg_1_1_out14), .In_3(n16bit_reg_1_1_out13),
    .In_4(n16bit_reg_1_1_out12), .In_5(n16bit_reg_1_1_out11), .In_6(n16bit_reg_1_1_out10),
    .In_7(n16bit_reg_1_1_out9), .In_8(n16bit_reg_1_1_out8), .In_9(n16bit_reg_1_1_out7),
    .In_10(n16bit_reg_1_1_out6), .In_11(n16bit_reg_1_1_out5), .In_12(n16bit_reg_1_1_out4),
    .In_13(n16bit_reg_1_1_out3), .In_14(n16bit_reg_1_1_out2), .In_15(n16bit_reg_1_1_out1),
    .In_16(n16bit_reg_1_1_out0), .Out(out_5));

  // Notes on the sheet:
  //   ADD+
endmodule

module gen_reg (
  input  [15:0] in_1,
  input  [2:0] in_2,
  input  in_3,
  output [15:0] out_4
);

  wire and_1_out, and_2_out, and_3_out, and_4_out, and_5_out, and_6_out, and_7_out, and_8_out, and_9_out,
       and_10_out, and_11_out, and_12_out, and_13_out, and_14_out, and_15_out, and_16_out,
       n16bit_reg_1_1_out0, n16bit_reg_1_1_out1, n16bit_reg_1_1_out2, n16bit_reg_1_1_out3,
       n16bit_reg_1_1_out4, n16bit_reg_1_1_out5, n16bit_reg_1_1_out6, n16bit_reg_1_1_out7,
       n16bit_reg_1_1_out8, n16bit_reg_1_1_out9, n16bit_reg_1_1_out10, n16bit_reg_1_1_out11,
       n16bit_reg_1_1_out12, n16bit_reg_1_1_out13, n16bit_reg_1_1_out14, n16bit_reg_1_1_out15,
       n16bit_reg_1_2_out0, n16bit_reg_1_2_out1, n16bit_reg_1_2_out2, n16bit_reg_1_2_out3,
       n16bit_reg_1_2_out4, n16bit_reg_1_2_out5, n16bit_reg_1_2_out6, n16bit_reg_1_2_out7,
       n16bit_reg_1_2_out8, n16bit_reg_1_2_out9, n16bit_reg_1_2_out10, n16bit_reg_1_2_out11,
       n16bit_reg_1_2_out12, n16bit_reg_1_2_out13, n16bit_reg_1_2_out14, n16bit_reg_1_2_out15,
       n16bit_reg_1_3_out0, n16bit_reg_1_3_out1, n16bit_reg_1_3_out2, n16bit_reg_1_3_out3,
       n16bit_reg_1_3_out4, n16bit_reg_1_3_out5, n16bit_reg_1_3_out6, n16bit_reg_1_3_out7,
       n16bit_reg_1_3_out8, n16bit_reg_1_3_out9, n16bit_reg_1_3_out10, n16bit_reg_1_3_out11,
       n16bit_reg_1_3_out12, n16bit_reg_1_3_out13, n16bit_reg_1_3_out14, n16bit_reg_1_3_out15,
       n16bit_reg_1_4_out0, n16bit_reg_1_4_out1, n16bit_reg_1_4_out2, n16bit_reg_1_4_out3,
       n16bit_reg_1_4_out4, n16bit_reg_1_4_out5, n16bit_reg_1_4_out6, n16bit_reg_1_4_out7,
       n16bit_reg_1_4_out8, n16bit_reg_1_4_out9, n16bit_reg_1_4_out10, n16bit_reg_1_4_out11,
       n16bit_reg_1_4_out12, n16bit_reg_1_4_out13, n16bit_reg_1_4_out14, n16bit_reg_1_4_out15,
       n16bit_reg_1_5_out0, n16bit_reg_1_5_out1, n16bit_reg_1_5_out2, n16bit_reg_1_5_out3,
       n16bit_reg_1_5_out4, n16bit_reg_1_5_out5, n16bit_reg_1_5_out6, n16bit_reg_1_5_out7,
       n16bit_reg_1_5_out8, n16bit_reg_1_5_out9, n16bit_reg_1_5_out10, n16bit_reg_1_5_out11,
       n16bit_reg_1_5_out12, n16bit_reg_1_5_out13, n16bit_reg_1_5_out14, n16bit_reg_1_5_out15,
       n16bit_reg_1_6_out0, n16bit_reg_1_6_out1, n16bit_reg_1_6_out2, n16bit_reg_1_6_out3,
       n16bit_reg_1_6_out4, n16bit_reg_1_6_out5, n16bit_reg_1_6_out6, n16bit_reg_1_6_out7,
       n16bit_reg_1_6_out8, n16bit_reg_1_6_out9, n16bit_reg_1_6_out10, n16bit_reg_1_6_out11,
       n16bit_reg_1_6_out12, n16bit_reg_1_6_out13, n16bit_reg_1_6_out14, n16bit_reg_1_6_out15,
       n16bit_reg_1_7_out0, n16bit_reg_1_7_out1, n16bit_reg_1_7_out2, n16bit_reg_1_7_out3,
       n16bit_reg_1_7_out4, n16bit_reg_1_7_out5, n16bit_reg_1_7_out6, n16bit_reg_1_7_out7,
       n16bit_reg_1_7_out8, n16bit_reg_1_7_out9, n16bit_reg_1_7_out10, n16bit_reg_1_7_out11,
       n16bit_reg_1_7_out12, n16bit_reg_1_7_out13, n16bit_reg_1_7_out14, n16bit_reg_1_7_out15,
       n16bit_reg_1_8_out0, n16bit_reg_1_8_out1, n16bit_reg_1_8_out2, n16bit_reg_1_8_out3,
       n16bit_reg_1_8_out4, n16bit_reg_1_8_out5, n16bit_reg_1_8_out6, n16bit_reg_1_8_out7,
       n16bit_reg_1_8_out8, n16bit_reg_1_8_out9, n16bit_reg_1_8_out10, n16bit_reg_1_8_out11,
       n16bit_reg_1_8_out12, n16bit_reg_1_8_out13, n16bit_reg_1_8_out14, n16bit_reg_1_8_out15;
  wire [15:0] n16bit_reg_selector_1_out, n16bit_reg_selector_2_out, n16bit_reg_selector_3_out,
       n16bit_reg_selector_4_out, n16bit_reg_selector_5_out, n16bit_reg_selector_6_out,
       n16bit_reg_selector_7_out, n16bit_reg_selector_8_out;

  and and_1 (and_1_out, ~in_2[0], ~in_2[1], ~in_2[2]);  // AND_Gate
  and and_2 (and_2_out, and_1_out, in_3);
  and and_3 (and_3_out, in_2[0], ~in_2[1], ~in_2[2]);  // AND_Gate
  and and_4 (and_4_out, and_3_out, in_3);
  and and_5 (and_5_out, ~in_2[0], in_2[1], ~in_2[2]);  // AND_Gate
  and and_6 (and_6_out, and_5_out, in_3);
  and and_7 (and_7_out, in_2[0], in_2[1], ~in_2[2]);  // AND_Gate
  and and_8 (and_8_out, and_7_out, in_3);
  and and_9 (and_9_out, ~in_2[0], ~in_2[1], in_2[2]);  // AND_Gate
  and and_10 (and_10_out, and_9_out, in_3);
  and and_11 (and_11_out, in_2[0], ~in_2[1], in_2[2]);  // AND_Gate
  and and_12 (and_12_out, and_11_out, in_3);
  and and_13 (and_13_out, ~in_2[0], in_2[1], in_2[2]);  // AND_Gate
  and and_14 (and_14_out, and_13_out, in_3);
  and and_15 (and_15_out, in_2[0], in_2[1], in_2[2]);
  and and_16 (and_16_out, and_15_out, in_3);
  _16bit_reg_1 u_16bit_reg_1_1 (
    .WE(and_2_out), .In(in_1), .Out15(n16bit_reg_1_1_out15), .Out14(n16bit_reg_1_1_out14),
    .Out13(n16bit_reg_1_1_out13), .Out12(n16bit_reg_1_1_out12), .Out11(n16bit_reg_1_1_out11),
    .Out10(n16bit_reg_1_1_out10), .Out9(n16bit_reg_1_1_out9), .Out8(n16bit_reg_1_1_out8),
    .Out7(n16bit_reg_1_1_out7), .Out6(n16bit_reg_1_1_out6), .Out5(n16bit_reg_1_1_out5),
    .Out4(n16bit_reg_1_1_out4), .Out3(n16bit_reg_1_1_out3), .Out2(n16bit_reg_1_1_out2),
    .Out1(n16bit_reg_1_1_out1), .Out0(n16bit_reg_1_1_out0));
  _16bit_reg_selector u_16bit_reg_selector_1 (
    .WE(and_1_out), .In(n16bit_reg_1_1_out15), .In_2(n16bit_reg_1_1_out14), .In_3(n16bit_reg_1_1_out13),
    .In_4(n16bit_reg_1_1_out12), .In_5(n16bit_reg_1_1_out11), .In_6(n16bit_reg_1_1_out10),
    .In_7(n16bit_reg_1_1_out9), .In_8(n16bit_reg_1_1_out8), .In_9(n16bit_reg_1_1_out7),
    .In_10(n16bit_reg_1_1_out6), .In_11(n16bit_reg_1_1_out5), .In_12(n16bit_reg_1_1_out4),
    .In_13(n16bit_reg_1_1_out3), .In_14(n16bit_reg_1_1_out2), .In_15(n16bit_reg_1_1_out1),
    .In_16(n16bit_reg_1_1_out0), .Out(n16bit_reg_selector_1_out));
  _16bit_reg_1 u_16bit_reg_1_2 (
    .WE(and_4_out), .In(in_1), .Out15(n16bit_reg_1_2_out15), .Out14(n16bit_reg_1_2_out14),
    .Out13(n16bit_reg_1_2_out13), .Out12(n16bit_reg_1_2_out12), .Out11(n16bit_reg_1_2_out11),
    .Out10(n16bit_reg_1_2_out10), .Out9(n16bit_reg_1_2_out9), .Out8(n16bit_reg_1_2_out8),
    .Out7(n16bit_reg_1_2_out7), .Out6(n16bit_reg_1_2_out6), .Out5(n16bit_reg_1_2_out5),
    .Out4(n16bit_reg_1_2_out4), .Out3(n16bit_reg_1_2_out3), .Out2(n16bit_reg_1_2_out2),
    .Out1(n16bit_reg_1_2_out1), .Out0(n16bit_reg_1_2_out0));
  _16bit_reg_selector u_16bit_reg_selector_2 (
    .WE(and_3_out), .In(n16bit_reg_1_2_out15), .In_2(n16bit_reg_1_2_out14), .In_3(n16bit_reg_1_2_out13),
    .In_4(n16bit_reg_1_2_out12), .In_5(n16bit_reg_1_2_out11), .In_6(n16bit_reg_1_2_out10),
    .In_7(n16bit_reg_1_2_out9), .In_8(n16bit_reg_1_2_out8), .In_9(n16bit_reg_1_2_out7),
    .In_10(n16bit_reg_1_2_out6), .In_11(n16bit_reg_1_2_out5), .In_12(n16bit_reg_1_2_out4),
    .In_13(n16bit_reg_1_2_out3), .In_14(n16bit_reg_1_2_out2), .In_15(n16bit_reg_1_2_out1),
    .In_16(n16bit_reg_1_2_out0), .Out(n16bit_reg_selector_2_out));
  _16bit_reg_1 u_16bit_reg_1_3 (
    .WE(and_6_out), .In(in_1), .Out15(n16bit_reg_1_3_out15), .Out14(n16bit_reg_1_3_out14),
    .Out13(n16bit_reg_1_3_out13), .Out12(n16bit_reg_1_3_out12), .Out11(n16bit_reg_1_3_out11),
    .Out10(n16bit_reg_1_3_out10), .Out9(n16bit_reg_1_3_out9), .Out8(n16bit_reg_1_3_out8),
    .Out7(n16bit_reg_1_3_out7), .Out6(n16bit_reg_1_3_out6), .Out5(n16bit_reg_1_3_out5),
    .Out4(n16bit_reg_1_3_out4), .Out3(n16bit_reg_1_3_out3), .Out2(n16bit_reg_1_3_out2),
    .Out1(n16bit_reg_1_3_out1), .Out0(n16bit_reg_1_3_out0));
  _16bit_reg_selector u_16bit_reg_selector_3 (
    .WE(and_5_out), .In(n16bit_reg_1_3_out15), .In_2(n16bit_reg_1_3_out14), .In_3(n16bit_reg_1_3_out13),
    .In_4(n16bit_reg_1_3_out12), .In_5(n16bit_reg_1_3_out11), .In_6(n16bit_reg_1_3_out10),
    .In_7(n16bit_reg_1_3_out9), .In_8(n16bit_reg_1_3_out8), .In_9(n16bit_reg_1_3_out7),
    .In_10(n16bit_reg_1_3_out6), .In_11(n16bit_reg_1_3_out5), .In_12(n16bit_reg_1_3_out4),
    .In_13(n16bit_reg_1_3_out3), .In_14(n16bit_reg_1_3_out2), .In_15(n16bit_reg_1_3_out1),
    .In_16(n16bit_reg_1_3_out0), .Out(n16bit_reg_selector_3_out));
  _16bit_reg_1 u_16bit_reg_1_4 (
    .WE(and_8_out), .In(in_1), .Out15(n16bit_reg_1_4_out15), .Out14(n16bit_reg_1_4_out14),
    .Out13(n16bit_reg_1_4_out13), .Out12(n16bit_reg_1_4_out12), .Out11(n16bit_reg_1_4_out11),
    .Out10(n16bit_reg_1_4_out10), .Out9(n16bit_reg_1_4_out9), .Out8(n16bit_reg_1_4_out8),
    .Out7(n16bit_reg_1_4_out7), .Out6(n16bit_reg_1_4_out6), .Out5(n16bit_reg_1_4_out5),
    .Out4(n16bit_reg_1_4_out4), .Out3(n16bit_reg_1_4_out3), .Out2(n16bit_reg_1_4_out2),
    .Out1(n16bit_reg_1_4_out1), .Out0(n16bit_reg_1_4_out0));
  _16bit_reg_selector u_16bit_reg_selector_4 (
    .WE(and_7_out), .In(n16bit_reg_1_4_out15), .In_2(n16bit_reg_1_4_out14), .In_3(n16bit_reg_1_4_out13),
    .In_4(n16bit_reg_1_4_out12), .In_5(n16bit_reg_1_4_out11), .In_6(n16bit_reg_1_4_out10),
    .In_7(n16bit_reg_1_4_out9), .In_8(n16bit_reg_1_4_out8), .In_9(n16bit_reg_1_4_out7),
    .In_10(n16bit_reg_1_4_out6), .In_11(n16bit_reg_1_4_out5), .In_12(n16bit_reg_1_4_out4),
    .In_13(n16bit_reg_1_4_out3), .In_14(n16bit_reg_1_4_out2), .In_15(n16bit_reg_1_4_out1),
    .In_16(n16bit_reg_1_4_out0), .Out(n16bit_reg_selector_4_out));
  _16bit_reg_1 u_16bit_reg_1_5 (
    .WE(and_10_out), .In(in_1), .Out15(n16bit_reg_1_5_out15), .Out14(n16bit_reg_1_5_out14),
    .Out13(n16bit_reg_1_5_out13), .Out12(n16bit_reg_1_5_out12), .Out11(n16bit_reg_1_5_out11),
    .Out10(n16bit_reg_1_5_out10), .Out9(n16bit_reg_1_5_out9), .Out8(n16bit_reg_1_5_out8),
    .Out7(n16bit_reg_1_5_out7), .Out6(n16bit_reg_1_5_out6), .Out5(n16bit_reg_1_5_out5),
    .Out4(n16bit_reg_1_5_out4), .Out3(n16bit_reg_1_5_out3), .Out2(n16bit_reg_1_5_out2),
    .Out1(n16bit_reg_1_5_out1), .Out0(n16bit_reg_1_5_out0));
  _16bit_reg_selector u_16bit_reg_selector_5 (
    .WE(and_9_out), .In(n16bit_reg_1_5_out15), .In_2(n16bit_reg_1_5_out14), .In_3(n16bit_reg_1_5_out13),
    .In_4(n16bit_reg_1_5_out12), .In_5(n16bit_reg_1_5_out11), .In_6(n16bit_reg_1_5_out10),
    .In_7(n16bit_reg_1_5_out9), .In_8(n16bit_reg_1_5_out8), .In_9(n16bit_reg_1_5_out7),
    .In_10(n16bit_reg_1_5_out6), .In_11(n16bit_reg_1_5_out5), .In_12(n16bit_reg_1_5_out4),
    .In_13(n16bit_reg_1_5_out3), .In_14(n16bit_reg_1_5_out2), .In_15(n16bit_reg_1_5_out1),
    .In_16(n16bit_reg_1_5_out0), .Out(n16bit_reg_selector_5_out));
  _16bit_reg_1 u_16bit_reg_1_6 (
    .WE(and_12_out), .In(in_1), .Out15(n16bit_reg_1_6_out15), .Out14(n16bit_reg_1_6_out14),
    .Out13(n16bit_reg_1_6_out13), .Out12(n16bit_reg_1_6_out12), .Out11(n16bit_reg_1_6_out11),
    .Out10(n16bit_reg_1_6_out10), .Out9(n16bit_reg_1_6_out9), .Out8(n16bit_reg_1_6_out8),
    .Out7(n16bit_reg_1_6_out7), .Out6(n16bit_reg_1_6_out6), .Out5(n16bit_reg_1_6_out5),
    .Out4(n16bit_reg_1_6_out4), .Out3(n16bit_reg_1_6_out3), .Out2(n16bit_reg_1_6_out2),
    .Out1(n16bit_reg_1_6_out1), .Out0(n16bit_reg_1_6_out0));
  _16bit_reg_selector u_16bit_reg_selector_6 (
    .WE(and_11_out), .In(n16bit_reg_1_6_out15), .In_2(n16bit_reg_1_6_out14), .In_3(n16bit_reg_1_6_out13),
    .In_4(n16bit_reg_1_6_out12), .In_5(n16bit_reg_1_6_out11), .In_6(n16bit_reg_1_6_out10),
    .In_7(n16bit_reg_1_6_out9), .In_8(n16bit_reg_1_6_out8), .In_9(n16bit_reg_1_6_out7),
    .In_10(n16bit_reg_1_6_out6), .In_11(n16bit_reg_1_6_out5), .In_12(n16bit_reg_1_6_out4),
    .In_13(n16bit_reg_1_6_out3), .In_14(n16bit_reg_1_6_out2), .In_15(n16bit_reg_1_6_out1),
    .In_16(n16bit_reg_1_6_out0), .Out(n16bit_reg_selector_6_out));
  _16bit_reg_1 u_16bit_reg_1_7 (
    .WE(and_14_out), .In(in_1), .Out15(n16bit_reg_1_7_out15), .Out14(n16bit_reg_1_7_out14),
    .Out13(n16bit_reg_1_7_out13), .Out12(n16bit_reg_1_7_out12), .Out11(n16bit_reg_1_7_out11),
    .Out10(n16bit_reg_1_7_out10), .Out9(n16bit_reg_1_7_out9), .Out8(n16bit_reg_1_7_out8),
    .Out7(n16bit_reg_1_7_out7), .Out6(n16bit_reg_1_7_out6), .Out5(n16bit_reg_1_7_out5),
    .Out4(n16bit_reg_1_7_out4), .Out3(n16bit_reg_1_7_out3), .Out2(n16bit_reg_1_7_out2),
    .Out1(n16bit_reg_1_7_out1), .Out0(n16bit_reg_1_7_out0));
  _16bit_reg_selector u_16bit_reg_selector_7 (
    .WE(and_13_out), .In(n16bit_reg_1_7_out15), .In_2(n16bit_reg_1_7_out14), .In_3(n16bit_reg_1_7_out13),
    .In_4(n16bit_reg_1_7_out12), .In_5(n16bit_reg_1_7_out11), .In_6(n16bit_reg_1_7_out10),
    .In_7(n16bit_reg_1_7_out9), .In_8(n16bit_reg_1_7_out8), .In_9(n16bit_reg_1_7_out7),
    .In_10(n16bit_reg_1_7_out6), .In_11(n16bit_reg_1_7_out5), .In_12(n16bit_reg_1_7_out4),
    .In_13(n16bit_reg_1_7_out3), .In_14(n16bit_reg_1_7_out2), .In_15(n16bit_reg_1_7_out1),
    .In_16(n16bit_reg_1_7_out0), .Out(n16bit_reg_selector_7_out));
  _16bit_reg_1 u_16bit_reg_1_8 (
    .WE(and_16_out), .In(in_1), .Out15(n16bit_reg_1_8_out15), .Out14(n16bit_reg_1_8_out14),
    .Out13(n16bit_reg_1_8_out13), .Out12(n16bit_reg_1_8_out12), .Out11(n16bit_reg_1_8_out11),
    .Out10(n16bit_reg_1_8_out10), .Out9(n16bit_reg_1_8_out9), .Out8(n16bit_reg_1_8_out8),
    .Out7(n16bit_reg_1_8_out7), .Out6(n16bit_reg_1_8_out6), .Out5(n16bit_reg_1_8_out5),
    .Out4(n16bit_reg_1_8_out4), .Out3(n16bit_reg_1_8_out3), .Out2(n16bit_reg_1_8_out2),
    .Out1(n16bit_reg_1_8_out1), .Out0(n16bit_reg_1_8_out0));
  _16bit_reg_selector u_16bit_reg_selector_8 (
    .WE(and_15_out), .In(n16bit_reg_1_8_out15), .In_2(n16bit_reg_1_8_out14), .In_3(n16bit_reg_1_8_out13),
    .In_4(n16bit_reg_1_8_out12), .In_5(n16bit_reg_1_8_out11), .In_6(n16bit_reg_1_8_out10),
    .In_7(n16bit_reg_1_8_out9), .In_8(n16bit_reg_1_8_out8), .In_9(n16bit_reg_1_8_out7),
    .In_10(n16bit_reg_1_8_out6), .In_11(n16bit_reg_1_8_out5), .In_12(n16bit_reg_1_8_out4),
    .In_13(n16bit_reg_1_8_out3), .In_14(n16bit_reg_1_8_out2), .In_15(n16bit_reg_1_8_out1),
    .In_16(n16bit_reg_1_8_out0), .Out(n16bit_reg_selector_8_out));
  assign out_4 = n16bit_reg_selector_1_out | n16bit_reg_selector_2_out | n16bit_reg_selector_3_out | n16bit_reg_selector_4_out | n16bit_reg_selector_5_out | n16bit_reg_selector_6_out | n16bit_reg_selector_7_out | n16bit_reg_selector_8_out;  // OR_Gate or_1, 16 bits wide
endmodule
