// Logisim project not_nor_or_nand_and.circ as structural Verilog: 1 circuit, main circuit main
module main (
  input  Input,
  input  Input_2,
  input  Input_3,
  input  A,
  input  A_2,
  input  in_6,
  input  B,
  input  B_2,
  input  A_3,
  input  _1in,
  input  _2in,
  input  _1in_2,
  input  _2in_2,
  input  _1in_3,
  input  _2in_3,
  input  _3in,
  input  A_4,
  input  _3in_2,
  input  A_5,
  input  A_6,
  input  B_3,
  input  _3in_3,
  input  B_4,
  input  B_5,
  input  C,
  output _1out,
  output _1out_2,
  output _1out_3,
  output _1out_4,
  output _1out_5,
  output _1out_6
);

  wire transistor_6_out, transistor_8_out, transistor_11_out, transistor_14_out, transistor_17_out,
       transistor_18_out, transistor_23_out, transistor_26_out, transistor_27_out;

  Transistor transistor_1 (.in(Input_3), .out(_1out), .gate(A_3));
  Transistor #(.\type ("n")) transistor_2 (.in(1'b0), .out(_1out), .gate(A_3));
  Transistor transistor_3 (.in(_1in), .out(_1out_4), .gate(A_4));
  Transistor transistor_4 (.in(_2in), .out(_1out_4), .gate(B_3));
  Transistor #(.\type ("n")) transistor_5 (.in(transistor_6_out), .out(_1out_4), .gate(A_4));
  Transistor #(.\type ("n")) transistor_6 (.in(1'b0), .out(transistor_6_out), .gate(B_3));
  Transistor #(.\type ("n")) transistor_7 (.in(1'b0), .out(_1out_2), .gate(B_2));
  Transistor transistor_8 (.in(Input_2), .out(transistor_8_out), .gate(A_2));
  Transistor transistor_9 (.in(transistor_8_out), .out(_1out_2), .gate(B_2));
  Transistor #(.\type ("n")) transistor_10 (.in(1'b0), .out(_1out_2), .gate(A_2));
  Transistor transistor_11 (.in(_1in_2), .out(transistor_11_out), .gate(A_5));
  Transistor transistor_12 (.in(_2in_2), .out(transistor_11_out), .gate(B_4));
  Transistor #(.\type ("n")) transistor_13 (.in(transistor_14_out), .out(transistor_11_out), .gate(A_5));
  Transistor #(.\type ("n")) transistor_14 (.in(1'b0), .out(transistor_14_out), .gate(B_4));
  Transistor transistor_15 (.in(_3in_2), .out(_1out_5), .gate(transistor_11_out));
  Transistor #(.\type ("n")) transistor_16 (.in(1'b0), .out(_1out_5), .gate(transistor_11_out));
  Transistor transistor_17 (.in(Input), .out(transistor_17_out), .gate(A));
  Transistor transistor_18 (.in(transistor_17_out), .out(transistor_18_out), .gate(B));
  Transistor #(.\type ("n")) transistor_19 (.in(1'b0), .out(transistor_18_out), .gate(B));
  Transistor transistor_20 (.in(in_6), .out(_1out_3), .gate(transistor_18_out));
  Transistor #(.\type ("n")) transistor_21 (.in(1'b0), .out(_1out_3), .gate(transistor_18_out));
  Transistor #(.\type ("n")) transistor_22 (.in(1'b0), .out(transistor_18_out), .gate(A));
  Transistor transistor_23 (.in(_2in_3), .out(transistor_23_out), .gate(B_5));
  Transistor transistor_24 (.in(_1in_3), .out(transistor_23_out), .gate(A_6));
  Transistor #(.\type ("n")) transistor_25 (.in(transistor_26_out), .out(transistor_23_out), .gate(A_6));
  Transistor #(.\type ("n")) transistor_26 (.in(transistor_27_out), .out(transistor_26_out), .gate(B_5));
  Transistor #(.\type ("n")) transistor_27 (.in(1'b0), .out(transistor_27_out), .gate(C));
  Transistor transistor_28 (.in(_3in), .out(transistor_23_out), .gate(C));
  Transistor transistor_29 (.in(_3in_3), .out(_1out_6), .gate(transistor_23_out));
  Transistor #(.\type ("n")) transistor_30 (.in(1'b0), .out(_1out_6), .gate(transistor_23_out));

  // Notes on the sheet:
  //   NOT Logic Gate
  //   NAND Logic Gate
  //   NOR Logic Gate
  //   AND Logic Gate
  //   OR Logic Gate
  //   3bit AND Logic Gate
endmodule
